// Logisim project 16bit-CPU-32ISA.circ as structural Verilog: 17 circuits, main circuit main
module main (
  input  ClearPC,
  input  Start,
  input  ManualClock
);

  wire alu_1_c_flag, alu_1_n_flag, alu_1_v_flag, alu_1_z_flag, and_1_out, and_2_out, and_3_out, clock_1_out,
       controllunit_1_data_mux, controllunit_1_datamem_en, controllunit_1_datamem_we,
       controllunit_1_dest_mux, controllunit_1_en_push, controllunit_1_en_shft, controllunit_1_enflagupdate,
       controllunit_1_func_mux, controllunit_1_hlt, controllunit_1_is_brh, controllunit_1_now,
       controllunit_1_pc_mux_bit0, controllunit_1_reg_rs2_mux, controllunit_1_regen, controllunit_1_rs2_mux,
       flagchecker_1_trueorfalse, not_1_out, or_2_out;
  wire [1:0] or_1_out;
  wire [4:0] controllunit_1_imm_operation_func, multiplexer_2_out, multiplexer_3_out, multiplexer_4_out,
       multiplexer_7_out;
  wire [15:0] alu_1_out_10, datamemory_1_out_6, multiplexer_5_out, multiplexer_6_out, regfile_1_r1out,
       regfile_1_r2out;
  wire [19:0] adder_1_out, callstack_1_popout, instmemory_1_instruction, multiplexer_1_out,
       programcounter_1_addr;
  wire [31:20] instmemory_1_instruction_2;

  Multiplexer #(.select(2), .width(20)) multiplexer_1 (
    .in0(adder_1_out), .in1(instmemory_1_instruction), .in2(callstack_1_popout), .in3({20{1'b0}}),
    .out(multiplexer_1_out), .sel(or_1_out));
  or or_1 (or_1_out[0], and_3_out, controllunit_1_pc_mux_bit0);
  ProgramCounter programcounter_1 (
    .Address_plus_1(multiplexer_1_out), .CLK(or_2_out), .CLR(ClearPC), .Addr(programcounter_1_addr));
  Clock clock_1 (.out(clock_1_out));
  Adder #(.width(20)) adder_1 (.a(programcounter_1_addr), .b({20{1'b0}}), .out(adder_1_out), .cin(1'b1));  // open: cout
  and and_1 (and_1_out, clock_1_out, and_2_out);
  and and_2 (and_2_out, Start, not_1_out);
  or or_2 (or_2_out, and_1_out, ManualClock);
  not not_1 (not_1_out, controllunit_1_hlt);
  CallStack callstack_1 (
    .DataInput(adder_1_out), .PopOrPush(controllunit_1_en_push), .CLK(or_2_out),
    .EnShift(controllunit_1_en_shft), .PopOut(callstack_1_popout));
  InstMemory instmemory_1 (
    .Addr(programcounter_1_addr), .Instruction({instmemory_1_instruction_2, instmemory_1_instruction}));
  ControllUnit controllunit_1 (
    .in_1(instmemory_1_instruction_2[31:26]), .Rs2_MUX(controllunit_1_rs2_mux),
    .Dest_MUX(controllunit_1_dest_mux), .RegEn(controllunit_1_regen), .HLT(controllunit_1_hlt),
    .PC_MUX_bit0(controllunit_1_pc_mux_bit0), .Is_BRH(controllunit_1_is_brh),
    .Func_MUX(controllunit_1_func_mux), .EN_SHFT(controllunit_1_en_shft), .EN_PUSH(controllunit_1_en_push),
    .PC_MUX_bit1(or_1_out[1]), .DataMem_EN(controllunit_1_datamem_en),
    .DataMem_WE(controllunit_1_datamem_we), .NoW(controllunit_1_now), .Data_MUX(controllunit_1_data_mux),
    .Reg_Rs2_MUX(controllunit_1_reg_rs2_mux), .Imm_operation_func(controllunit_1_imm_operation_func),
    .EnFlagUpdate(controllunit_1_enflagupdate));
  Multiplexer #(.width(5)) multiplexer_2 (
    .in0({instmemory_1_instruction_2[20], instmemory_1_instruction[19:16]}),
    .in1(instmemory_1_instruction[4:0]), .out(multiplexer_2_out), .sel(controllunit_1_reg_rs2_mux));
  Multiplexer #(.width(5)) multiplexer_3 (
    .in0(instmemory_1_instruction[15:11]), .in1(instmemory_1_instruction[4:0]), .out(multiplexer_3_out),
    .sel(controllunit_1_dest_mux));
  Multiplexer #(.width(5)) multiplexer_4 (
    .in0(multiplexer_3_out), .in1({5{1'b0}}), .out(multiplexer_4_out), .sel(controllunit_1_now));
  Multiplexer #(.width(16)) multiplexer_5 (
    .in0(alu_1_out_10), .in1(datamemory_1_out_6), .out(multiplexer_5_out), .sel(controllunit_1_data_mux));
  RegFile regfile_1 (
    .En(controllunit_1_regen), .CLK(or_2_out), .W(multiplexer_4_out), .R1(instmemory_1_instruction_2[25:21]),
    .R2(multiplexer_2_out), .Data(multiplexer_5_out), .R1OUT(regfile_1_r1out), .R2Out(regfile_1_r2out));
  Multiplexer #(.width(16)) multiplexer_6 (
    .in0(regfile_1_r2out), .in1({instmemory_1_instruction_2[20], instmemory_1_instruction[19:5]}),
    .out(multiplexer_6_out), .sel(controllunit_1_rs2_mux));
  Multiplexer #(.width(5)) multiplexer_7 (
    .in0(instmemory_1_instruction[4:0]), .in1(controllunit_1_imm_operation_func), .out(multiplexer_7_out),
    .sel(controllunit_1_func_mux));
  DataMemory datamemory_1 (
    .CLK(or_2_out), .EN(controllunit_1_datamem_en), .Address(alu_1_out_10), .Data(regfile_1_r2out),
    .WE(controllunit_1_datamem_we), .out_6(datamemory_1_out_6));
  ALU alu_1 (
    .Rs1(regfile_1_r1out), .Rs2(multiplexer_6_out), .EnFlagUpdate(controllunit_1_enflagupdate),
    .func(multiplexer_7_out), .Clock_Signal(or_2_out), .out_10(alu_1_out_10), .C_Flag(alu_1_c_flag),
    .Z_Flag(alu_1_z_flag), .V_Flag(alu_1_v_flag), .N_Flag(alu_1_n_flag));
  FlagChecker flagchecker_1 (
    .V_Flag(alu_1_v_flag), .N_Flag(alu_1_n_flag), .C_Flag(alu_1_c_flag), .Z_Flag(alu_1_z_flag),
    .COND(instmemory_1_instruction_2[25:22]), .TrueOrFalse(flagchecker_1_trueorfalse));
  and and_3 (and_3_out, flagchecker_1_trueorfalse, controllunit_1_is_brh);

  // Notes on the sheet:
  //   Func
  //   Opcode
endmodule

module ALU (
  input  [4:0] func,
  input  Clock_Signal,
  input  [15:0] Rs1,
  input  [15:0] Rs2,
  input  EnFlagUpdate,
  output V_Flag,
  output N_Flag,
  output C_Flag,
  output Z_Flag,
  output [15:0] out_10
);

  wire add_v_out, adder_1_cout, adder_2_cout, and_1_out, and_2_out, and_3_out, and_4_out, Carry_out,
       decoder_1_out0, decoder_1_out1, decoder_1_out2, decoder_1_out3, decoder_1_out4, decoder_1_out5,
       decoder_1_out6, decoder_1_out7, decoder_1_out8, multiplexer_1_out, multiplexer_2_out, Negative_out,
       not_1_out, or_1_out, Overflow_out, sub_v_out, subtractor_1_bout, subtractor_2_bout, Zero_out;
  wire [15:0] adder_1_out, bitwiseand_1_out_3, bitwisenor_1_out_3, bitwisenot_1_out_2, bitwiseor_1_out_3,
       bitwisexor_1_out_3, divider_1_out, divider_1_rem, divider_2_out, divider_2_rem, shifter_1_out,
       shifter_2_out, shifter_3_out, subtractor_1_out;
  wire [31:0] multiplier_1_out, multiplier_2_out;

  Adder #(.width(16)) adder_1 (.a(Rs1), .b(Rs2), .out(adder_1_out), .cout(adder_1_cout));  // open: cin
  Subtractor #(.width(16)) subtractor_1 (
    .a(Rs1), .b(Rs2), .out(subtractor_1_out), .bout(subtractor_1_bout));  // open: bin
  BitwiseAND bitwiseand_1 (.A(Rs1), .B(Rs2), .out_3(bitwiseand_1_out_3));
  BitwiseOR bitwiseor_1 (.A(Rs1), .B(Rs2), .out_3(bitwiseor_1_out_3));
  BitwiseXOR bitwisexor_1 (.A(Rs1), .B(Rs2), .out_3(bitwisexor_1_out_3));
  BitwiseNOR bitwisenor_1 (.A(Rs1), .B(Rs2), .out_3(bitwisenor_1_out_3));
  Shifter #(.width(16)) shifter_1 (.in(Rs2), .\dist (Rs1[3:0]), .out(shifter_1_out));
  Shifter #(.shift("lr"), .width(16)) shifter_2 (.in(Rs2), .\dist (Rs1[3:0]), .out(shifter_2_out));
  Shifter #(.shift("ar"), .width(16)) shifter_3 (.in(Rs2), .\dist (Rs1[3:0]), .out(shifter_3_out));
  Multiplier #(.mode("twosComplement"), .width(32)) multiplier_1 (
    .a({{17{Rs1[15]}}, Rs1[14:0]}), .b({{17{Rs2[15]}}, Rs2[14:0]}), .out(multiplier_1_out));  // open: cin, cout
  Multiplier #(.width(32)) multiplier_2 (
    .a({{16{1'b0}}, Rs1}), .b({{16{1'b0}}, Rs2}), .out(multiplier_2_out));  // open: cin, cout
  Divider #(.mode("twosComplement"), .width(16)) divider_1 (
    .a(Rs1), .b(Rs2), .out(divider_1_out), .rem(divider_1_rem));  // open: upper
  Divider #(.width(16)) divider_2 (.a(Rs1), .b(Rs2), .out(divider_2_out), .rem(divider_2_rem));  // open: upper
  BitwiseNOT bitwisenot_1 (.B(Rs2), .out_2(bitwisenot_1_out_2));
  Adder #(.width(15)) adder_2 (.a(Rs1[14:0]), .b(Rs2[14:0]), .cout(adder_2_cout));  // open: out, cin
  xor add_v (add_v_out, adder_2_cout, adder_1_cout);
  Subtractor #(.width(15)) subtractor_2 (.a(Rs1[14:0]), .b(Rs2[14:0]), .bout(subtractor_2_bout));  // open: out, bin
  xor sub_v (sub_v_out, subtractor_2_bout, subtractor_1_bout);
  Multiplexer #(.select(5)) multiplexer_1 (
    .in0(adder_1_cout), .in1(subtractor_1_bout), .in2(1'b0), .in3(1'b0), .in4(1'b0), .in5(1'b0), .in6(1'b0),
    .in7(1'b0), .in8(1'b0), .in9(1'b0), .in10(1'b0), .in11(1'b0), .in12(1'b0), .in13(1'b0), .in14(1'b0),
    .in15(1'b0), .in16(1'b0), .in17(1'b0), .in18(1'b0), .in19(1'b0), .in20(1'b0), .in21(1'b0), .in22(1'b0),
    .in23(1'b0), .in24(1'b0), .in25(1'b0), .in26(1'b0), .in27(1'b0), .in28(1'b0), .in29(1'b0), .in30(1'b0),
    .in31(1'b0), .out(multiplexer_1_out), .sel(func));
  Multiplexer #(.select(5)) multiplexer_2 (
    .in0(add_v_out), .in1(sub_v_out), .in2(1'b0), .in3(1'b0), .in4(1'b0), .in5(1'b0), .in6(1'b0), .in7(1'b0),
    .in8(1'b0), .in9(1'b0), .in10(1'b0), .in11(1'b0), .in12(1'b0), .in13(1'b0), .in14(1'b0), .in15(1'b0),
    .in16(1'b0), .in17(1'b0), .in18(1'b0), .in19(1'b0), .in20(1'b0), .in21(1'b0), .in22(1'b0), .in23(1'b0),
    .in24(1'b0), .in25(1'b0), .in26(1'b0), .in27(1'b0), .in28(1'b0), .in29(1'b0), .in30(1'b0), .in31(1'b0),
    .out(multiplexer_2_out), .sel(func));
  Multiplexer #(.select(5), .width(16)) multiplexer_3 (
    .in0(adder_1_out), .in1(subtractor_1_out), .in2(bitwiseand_1_out_3), .in3(bitwiseor_1_out_3),
    .in4(bitwisexor_1_out_3), .in5(bitwisenor_1_out_3), .in6(shifter_1_out), .in7(shifter_2_out),
    .in8(shifter_3_out), .in9(multiplier_1_out[15:0]), .in10(multiplier_1_out[31:16]),
    .in11(multiplier_2_out[15:0]), .in12(multiplier_2_out[31:16]), .in13(divider_1_out),
    .in14(divider_2_out), .in15(divider_1_rem), .in16(divider_2_rem), .in17(bitwisenot_1_out_2),
    .out(out_10), .sel(func));  // open: in18, in19, in20, in21, in22, in23, in24, in25, in26, in27, in28, in29, in30, in31
  Decoder #(.select(5)) decoder_1 (
    .out0(decoder_1_out0), .out1(decoder_1_out1), .out2(decoder_1_out2), .out3(decoder_1_out3),
    .out4(decoder_1_out4), .out5(decoder_1_out5), .out6(decoder_1_out6), .out7(decoder_1_out7),
    .out8(decoder_1_out8), .sel(func), .en(EnFlagUpdate));  // open: out9, out10, out11, out12, out13, out14, out15, out16, out17, out18, out19, out20, out21, out22, out23, out24, out25, out26, out27, out28, out29, out30, out31
  or or_1 (or_1_out, out_10[0], out_10[1], out_10[2], out_10[3], out_10[4], out_10[5], out_10[6], out_10[7], out_10[8], out_10[9], out_10[10], out_10[11], out_10[12], out_10[13], out_10[14], out_10[15]);
  not not_1 (not_1_out, or_1_out);
  or Overflow (Overflow_out, decoder_1_out0, decoder_1_out1);
  or Negative (Negative_out, decoder_1_out0, decoder_1_out1, decoder_1_out2, decoder_1_out3, decoder_1_out4, decoder_1_out5, decoder_1_out6, decoder_1_out7, decoder_1_out8);
  or Carry (Carry_out, decoder_1_out0, decoder_1_out1);
  or Zero (Zero_out, decoder_1_out0, decoder_1_out1, decoder_1_out2, decoder_1_out3, decoder_1_out4, decoder_1_out5, decoder_1_out6, decoder_1_out7, decoder_1_out8);
  Register #(.width(1)) register_1 (.D(multiplexer_2_out), .en(1'b1), .clk(and_1_out), .Q(V_Flag));  // open: clr
  Register #(.width(1)) register_2 (.D(out_10[15]), .en(1'b1), .clk(and_2_out), .Q(N_Flag));  // open: clr
  Register #(.width(1)) register_3 (.D(multiplexer_1_out), .en(1'b1), .clk(and_3_out), .Q(C_Flag));  // open: clr
  Register #(.width(1)) register_4 (.D(not_1_out), .en(1'b1), .clk(and_4_out), .Q(Z_Flag));  // open: clr
  and and_1 (and_1_out, Clock_Signal, Overflow_out);
  and and_2 (and_2_out, Clock_Signal, Negative_out);
  and and_3 (and_3_out, Clock_Signal, Carry_out);
  and and_4 (and_4_out, Clock_Signal, Zero_out);

  // Notes on the sheet:
  //   Overflow Flag
  //   Zero Flag
  //   Negative Flag
  //   Carry Flag
endmodule

module BitwiseAND (
  input  [15:0] A,
  input  [15:0] B,
  output [15:0] out_3
);

  and and_1 (out_3[0], A[0], B[0]);
  and and_2 (out_3[1], A[1], B[1]);
  and and_3 (out_3[2], A[2], B[2]);
  and and_4 (out_3[3], A[3], B[3]);
  and and_5 (out_3[4], A[4], B[4]);
  and and_6 (out_3[5], A[5], B[5]);
  and and_7 (out_3[6], A[6], B[6]);
  and and_8 (out_3[7], B[7], A[7]);
  and and_9 (out_3[8], A[8], B[8]);
  and and_10 (out_3[9], A[9], B[9]);
  and and_11 (out_3[10], A[10], B[10]);
  and and_12 (out_3[11], A[11], B[11]);
  and and_13 (out_3[12], A[12], B[12]);
  and and_14 (out_3[13], A[13], B[13]);
  and and_15 (out_3[14], A[14], B[14]);
  and and_16 (out_3[15], A[15], B[15]);
endmodule

module BitwiseOR (
  input  [15:0] A,
  input  [15:0] B,
  output [15:0] out_3
);

  or or_1 (out_3[0], A[0], B[0]);
  or or_2 (out_3[1], A[1], B[1]);
  or or_3 (out_3[2], A[2], B[2]);
  or or_4 (out_3[3], A[3], B[3]);
  or or_5 (out_3[4], A[4], B[4]);
  or or_6 (out_3[5], A[5], B[5]);
  or or_7 (out_3[6], A[6], B[6]);
  or or_8 (out_3[7], B[7], A[7]);
  or or_9 (out_3[8], A[8], B[8]);
  or or_10 (out_3[9], A[9], B[9]);
  or or_11 (out_3[10], A[10], B[10]);
  or or_12 (out_3[11], A[11], B[11]);
  or or_13 (out_3[12], A[12], B[12]);
  or or_14 (out_3[13], A[13], B[13]);
  or or_15 (out_3[14], A[14], B[14]);
  or or_16 (out_3[15], A[15], B[15]);
endmodule

module BitwiseXOR (
  input  [15:0] A,
  input  [15:0] B,
  output [15:0] out_3
);

  xor xor_1 (out_3[0], A[0], B[0]);
  xor xor_2 (out_3[1], A[1], B[1]);
  xor xor_3 (out_3[2], A[2], B[2]);
  xor xor_4 (out_3[3], A[3], B[3]);
  xor xor_5 (out_3[4], A[4], B[4]);
  xor xor_6 (out_3[5], A[5], B[5]);
  xor xor_7 (out_3[6], A[6], B[6]);
  xor xor_8 (out_3[7], B[7], A[7]);
  xor xor_9 (out_3[8], A[8], B[8]);
  xor xor_10 (out_3[9], A[9], B[9]);
  xor xor_11 (out_3[10], A[10], B[10]);
  xor xor_12 (out_3[11], A[11], B[11]);
  xor xor_13 (out_3[12], A[12], B[12]);
  xor xor_14 (out_3[13], A[13], B[13]);
  xor xor_15 (out_3[14], A[14], B[14]);
  xor xor_16 (out_3[15], A[15], B[15]);
endmodule

module BitwiseNOR (
  input  [15:0] A,
  input  [15:0] B,
  output [15:0] out_3
);

  nor nor_1 (out_3[0], A[0], B[0]);
  nor nor_2 (out_3[1], A[1], B[1]);
  nor nor_3 (out_3[2], A[2], B[2]);
  nor nor_4 (out_3[3], A[3], B[3]);
  nor nor_5 (out_3[4], A[4], B[4]);
  nor nor_6 (out_3[5], A[5], B[5]);
  nor nor_7 (out_3[6], A[6], B[6]);
  nor nor_8 (out_3[7], B[7], A[7]);
  nor nor_9 (out_3[8], A[8], B[8]);
  nor nor_10 (out_3[9], A[9], B[9]);
  nor nor_11 (out_3[10], A[10], B[10]);
  nor nor_12 (out_3[11], A[11], B[11]);
  nor nor_13 (out_3[12], A[12], B[12]);
  nor nor_14 (out_3[13], A[13], B[13]);
  nor nor_15 (out_3[14], A[14], B[14]);
  nor nor_16 (out_3[15], A[15], B[15]);
endmodule

module BitwiseNOT (
  input  [15:0] B,
  output [15:0] out_2
);

  not not_1 (out_2[0], B[0]);
  not not_2 (out_2[1], B[1]);
  not not_3 (out_2[2], B[2]);
  not not_4 (out_2[3], B[3]);
  not not_5 (out_2[4], B[4]);
  not not_6 (out_2[5], B[5]);
  not not_7 (out_2[6], B[6]);
  not not_8 (out_2[7], B[7]);
  not not_9 (out_2[8], B[8]);
  not not_10 (out_2[9], B[9]);
  not not_11 (out_2[10], B[10]);
  not not_12 (out_2[11], B[11]);
  not not_13 (out_2[12], B[12]);
  not not_14 (out_2[13], B[13]);
  not not_15 (out_2[14], B[14]);
  not not_16 (out_2[15], B[15]);
endmodule

module RegFile (
  input  En,
  input  [15:0] Data,
  input  [4:0] W,
  input  [4:0] R1,
  input  [4:0] R2,
  input  CLK,
  output [15:0] R1OUT,
  output [15:0] R2Out
);

  wire decoder_1_out1, decoder_1_out2, decoder_1_out3, decoder_1_out4, decoder_1_out5, decoder_1_out6,
       decoder_1_out7, decoder_1_out8, decoder_1_out9, decoder_1_out10, decoder_1_out11, decoder_1_out12,
       decoder_1_out13, decoder_1_out14, decoder_1_out15, decoder_1_out16, decoder_1_out17, decoder_1_out18,
       decoder_1_out19, decoder_1_out20, decoder_1_out21, decoder_1_out22, decoder_1_out23, decoder_1_out24,
       decoder_1_out25, decoder_1_out26, decoder_1_out27, decoder_1_out28, decoder_1_out29, decoder_1_out30,
       decoder_1_out31, decoder_2_out1, decoder_2_out2, decoder_2_out3, decoder_2_out4, decoder_2_out5,
       decoder_2_out6, decoder_2_out7, decoder_2_out8, decoder_2_out9, decoder_2_out10, decoder_2_out11,
       decoder_2_out12, decoder_2_out13, decoder_2_out14, decoder_2_out15, decoder_2_out16, decoder_2_out17,
       decoder_2_out18, decoder_2_out19, decoder_2_out20, decoder_2_out21, decoder_2_out22, decoder_2_out23,
       decoder_2_out24, decoder_2_out25, decoder_2_out26, decoder_2_out27, decoder_2_out28, decoder_2_out29,
       decoder_2_out30, decoder_2_out31, decoder_3_out1, decoder_3_out2, decoder_3_out3, decoder_3_out4,
       decoder_3_out5, decoder_3_out6, decoder_3_out7, decoder_3_out8, decoder_3_out9, decoder_3_out10,
       decoder_3_out11, decoder_3_out12, decoder_3_out13, decoder_3_out14, decoder_3_out15, decoder_3_out16,
       decoder_3_out17, decoder_3_out18, decoder_3_out19, decoder_3_out20, decoder_3_out21, decoder_3_out22,
       decoder_3_out23, decoder_3_out24, decoder_3_out25, decoder_3_out26, decoder_3_out27, decoder_3_out28,
       decoder_3_out29, decoder_3_out30, decoder_3_out31, decoder_4_out1, decoder_4_out2, decoder_4_out3,
       decoder_4_out4, decoder_4_out5, decoder_4_out6, decoder_4_out7, decoder_4_out8, decoder_4_out9,
       decoder_4_out10, decoder_4_out11, decoder_4_out12, decoder_4_out13, decoder_4_out14, decoder_4_out15,
       decoder_4_out16, decoder_4_out17, decoder_4_out18, decoder_4_out19, decoder_4_out20, decoder_4_out21,
       decoder_4_out22, decoder_4_out23, decoder_4_out24, decoder_4_out25, decoder_4_out26, decoder_4_out27,
       decoder_4_out28, decoder_4_out29, decoder_4_out30, decoder_4_out31, not_1_out, not_2_out, not_3_out,
       not_4_out, not_5_out, not_6_out, not_7_out, not_8_out, not_9_out, not_10_out, not_11_out, not_12_out,
       not_13_out, not_14_out, not_15_out, not_16_out, not_17_out, not_18_out, not_19_out, not_20_out,
       not_21_out, not_22_out, not_23_out, not_24_out, not_25_out, not_26_out, not_27_out, not_28_out,
       not_29_out, not_30_out, not_31_out, not_32_out, not_33_out, not_34_out, not_35_out, not_36_out,
       not_37_out, not_38_out, not_39_out, not_40_out, not_41_out, not_42_out, not_43_out, not_44_out,
       not_45_out, not_46_out, not_47_out, not_48_out, not_49_out, not_50_out, not_51_out, not_52_out,
       not_53_out, not_54_out, not_55_out, not_56_out, not_57_out, not_58_out, not_59_out, not_60_out,
       not_61_out, not_62_out;
  wire [15:0] cancler_1_out_3, cancler_2_out_3, cancler_3_out_3, cancler_4_out_3, cancler_5_out_3,
       cancler_6_out_3, cancler_7_out_3, cancler_8_out_3, cancler_9_out_3, cancler_10_out_3,
       cancler_11_out_3, cancler_12_out_3, cancler_13_out_3, cancler_14_out_3, cancler_16_out_3,
       cancler_17_out_3, cancler_18_out_3, cancler_19_out_3, cancler_20_out_3, cancler_21_out_3,
       cancler_22_out_3, cancler_24_out_3, cancler_25_out_3, cancler_26_out_3, cancler_27_out_3,
       cancler_28_out_3, cancler_29_out_3, cancler_30_out_3, cancler_32_out_3, cancler_33_out_3,
       cancler_34_out_3, cancler_35_out_3, cancler_36_out_3, cancler_37_out_3, cancler_38_out_3,
       cancler_39_out_3, cancler_40_out_3, cancler_41_out_3, cancler_42_out_3, cancler_43_out_3,
       cancler_44_out_3, cancler_45_out_3, cancler_47_out_3, cancler_48_out_3, cancler_49_out_3,
       cancler_50_out_3, cancler_51_out_3, cancler_52_out_3, cancler_53_out_3, cancler_55_out_3,
       cancler_56_out_3, cancler_57_out_3, cancler_58_out_3, cancler_59_out_3, cancler_60_out_3,
       cancler_61_out_3, or_2_out, or_3_out, or_4_out, or_5_out, or_6_out, or_8_out, or_9_out, or_10_out,
       Reg1_q, Reg2_q, Reg3_q, Reg4_q, Reg5_q, Reg6_q, Reg7_q, register_1_q, register_2_q, register_3_q,
       register_4_q, register_5_q, register_6_q, register_7_q, register_8_q, register_9_q, register_10_q,
       register_11_q, register_12_q, register_13_q, register_14_q, register_15_q, register_16_q,
       register_17_q, register_18_q, register_19_q, register_20_q, register_21_q, register_22_q,
       register_23_q, register_24_q, register_25_q, register_26_q, register_27_q, register_28_q,
       register_29_q, register_30_q, register_31_q, register_32_q, register_33_q, register_34_q,
       register_35_q, register_36_q, register_37_q, register_38_q, register_39_q, register_40_q,
       register_41_q, register_42_q, register_43_q, register_44_q, register_45_q, register_46_q,
       register_47_q, register_48_q, register_49_q, register_50_q, register_51_q, register_52_q,
       register_53_q, register_54_q, register_55_q;

  Decoder #(.select(5)) decoder_1 (
    .out1(decoder_1_out1), .out2(decoder_1_out2), .out3(decoder_1_out3), .out4(decoder_1_out4),
    .out5(decoder_1_out5), .out6(decoder_1_out6), .out7(decoder_1_out7), .out8(decoder_1_out8),
    .out9(decoder_1_out9), .out10(decoder_1_out10), .out11(decoder_1_out11), .out12(decoder_1_out12),
    .out13(decoder_1_out13), .out14(decoder_1_out14), .out15(decoder_1_out15), .out16(decoder_1_out16),
    .out17(decoder_1_out17), .out18(decoder_1_out18), .out19(decoder_1_out19), .out20(decoder_1_out20),
    .out21(decoder_1_out21), .out22(decoder_1_out22), .out23(decoder_1_out23), .out24(decoder_1_out24),
    .out25(decoder_1_out25), .out26(decoder_1_out26), .out27(decoder_1_out27), .out28(decoder_1_out28),
    .out29(decoder_1_out29), .out30(decoder_1_out30), .out31(decoder_1_out31), .sel(W), .en(En));  // open: out0
  Decoder #(.select(5)) decoder_2 (
    .out1(decoder_2_out1), .out2(decoder_2_out2), .out3(decoder_2_out3), .out4(decoder_2_out4),
    .out5(decoder_2_out5), .out6(decoder_2_out6), .out7(decoder_2_out7), .out8(decoder_2_out8),
    .out9(decoder_2_out9), .out10(decoder_2_out10), .out11(decoder_2_out11), .out12(decoder_2_out12),
    .out13(decoder_2_out13), .out14(decoder_2_out14), .out15(decoder_2_out15), .out16(decoder_2_out16),
    .out17(decoder_2_out17), .out18(decoder_2_out18), .out19(decoder_2_out19), .out20(decoder_2_out20),
    .out21(decoder_2_out21), .out22(decoder_2_out22), .out23(decoder_2_out23), .out24(decoder_2_out24),
    .out25(decoder_2_out25), .out26(decoder_2_out26), .out27(decoder_2_out27), .out28(decoder_2_out28),
    .out29(decoder_2_out29), .out30(decoder_2_out30), .out31(decoder_2_out31), .sel(R1), .en(En));  // open: out0
  not not_1 (not_1_out, decoder_2_out1);
  not not_2 (not_2_out, decoder_2_out2);
  not not_3 (not_3_out, decoder_2_out3);
  not not_4 (not_4_out, decoder_2_out4);
  not not_5 (not_5_out, decoder_2_out5);
  not not_6 (not_6_out, decoder_2_out6);
  not not_7 (not_7_out, decoder_2_out7);
  not not_8 (not_8_out, decoder_2_out8);
  not not_9 (not_9_out, decoder_2_out9);
  not not_10 (not_10_out, decoder_2_out10);
  not not_11 (not_11_out, decoder_2_out11);
  not not_12 (not_12_out, decoder_2_out12);
  not not_13 (not_13_out, decoder_2_out13);
  not not_14 (not_14_out, decoder_2_out14);
  not not_15 (not_15_out, decoder_2_out15);
  not not_16 (not_16_out, decoder_2_out16);
  not not_17 (not_17_out, decoder_2_out17);
  not not_18 (not_18_out, decoder_2_out18);
  not not_19 (not_19_out, decoder_2_out19);
  not not_20 (not_20_out, decoder_2_out20);
  not not_21 (not_21_out, decoder_2_out21);
  not not_22 (not_22_out, decoder_2_out22);
  not not_23 (not_23_out, decoder_2_out23);
  not not_24 (not_24_out, decoder_2_out24);
  not not_25 (not_25_out, decoder_2_out25);
  not not_26 (not_26_out, decoder_2_out26);
  not not_27 (not_27_out, decoder_2_out27);
  not not_28 (not_28_out, decoder_2_out28);
  not not_29 (not_29_out, decoder_2_out29);
  not not_30 (not_30_out, decoder_2_out30);
  not not_31 (not_31_out, decoder_2_out31);
  Register #(.width(16)) Reg7 (.D(Data), .en(decoder_1_out7), .clk(CLK), .Q(Reg7_q));  // open: clr
  Register #(.width(16)) Reg6 (.D(Data), .en(decoder_1_out6), .clk(CLK), .Q(Reg6_q));  // open: clr
  Register #(.width(16)) Reg5 (.D(Data), .en(decoder_1_out5), .clk(CLK), .Q(Reg5_q));  // open: clr
  Register #(.width(16)) Reg4 (.D(Data), .en(decoder_1_out4), .clk(CLK), .Q(Reg4_q));  // open: clr
  Register #(.width(16)) Reg3 (.D(Data), .en(decoder_1_out3), .clk(CLK), .Q(Reg3_q));  // open: clr
  Register #(.width(16)) Reg2 (.D(Data), .en(decoder_1_out2), .clk(CLK), .Q(Reg2_q));  // open: clr
  Register #(.width(16)) Reg1 (.D(Data), .en(decoder_1_out1), .clk(CLK), .Q(Reg1_q));  // open: clr
  Cancler cancler_1 (.Cancle(not_7_out), .Data(Reg7_q), .out_3(cancler_1_out_3));
  Cancler cancler_2 (.Cancle(not_6_out), .Data(Reg6_q), .out_3(cancler_2_out_3));
  Cancler cancler_3 (.Cancle(not_5_out), .Data(Reg5_q), .out_3(cancler_3_out_3));
  Cancler cancler_4 (.Cancle(not_4_out), .Data(Reg4_q), .out_3(cancler_4_out_3));
  Cancler cancler_5 (.Cancle(not_3_out), .Data(Reg3_q), .out_3(cancler_5_out_3));
  Cancler cancler_6 (.Cancle(not_2_out), .Data(Reg2_q), .out_3(cancler_6_out_3));
  Cancler cancler_7 (.Cancle(not_1_out), .Data(Reg1_q), .out_3(cancler_7_out_3));
  assign R1OUT = or_2_out | or_3_out | or_4_out | or_5_out;  // OR_Gate or_1, 16 bits wide
  assign or_2_out = cancler_1_out_3 | cancler_2_out_3 | cancler_3_out_3 | cancler_4_out_3 | cancler_5_out_3 | cancler_6_out_3 | cancler_7_out_3;  // OR_Gate or_2, 16 bits wide
  Register #(.width(16)) register_1 (.D(Data), .en(decoder_1_out15), .clk(CLK), .Q(register_1_q));  // open: clr
  Register #(.width(16)) register_2 (.D(Data), .en(decoder_1_out14), .clk(CLK), .Q(register_2_q));  // open: clr
  Register #(.width(16)) register_3 (.D(Data), .en(decoder_1_out13), .clk(CLK), .Q(register_3_q));  // open: clr
  Register #(.width(16)) register_4 (.D(Data), .en(decoder_1_out12), .clk(CLK), .Q(register_4_q));  // open: clr
  Register #(.width(16)) register_5 (.D(Data), .en(decoder_1_out11), .clk(CLK), .Q(register_5_q));  // open: clr
  Register #(.width(16)) register_6 (.D(Data), .en(decoder_1_out10), .clk(CLK), .Q(register_6_q));  // open: clr
  Register #(.width(16)) register_7 (.D(Data), .en(decoder_1_out9), .clk(CLK), .Q(register_7_q));  // open: clr
  Register #(.width(16)) register_8 (.D(Data), .en(decoder_1_out8), .clk(CLK), .Q(register_8_q));  // open: clr
  Cancler cancler_8 (.Cancle(not_15_out), .Data(register_1_q), .out_3(cancler_8_out_3));
  Cancler cancler_9 (.Cancle(not_14_out), .Data(register_2_q), .out_3(cancler_9_out_3));
  Cancler cancler_10 (.Cancle(not_13_out), .Data(register_3_q), .out_3(cancler_10_out_3));
  Cancler cancler_11 (.Cancle(not_12_out), .Data(register_4_q), .out_3(cancler_11_out_3));
  Cancler cancler_12 (.Cancle(not_11_out), .Data(register_5_q), .out_3(cancler_12_out_3));
  Cancler cancler_13 (.Cancle(not_10_out), .Data(register_6_q), .out_3(cancler_13_out_3));
  Cancler cancler_14 (.Cancle(not_9_out), .Data(register_7_q), .out_3(cancler_14_out_3));
  Cancler cancler_15 (.Cancle(not_8_out), .Data(register_8_q), .out_3(cancler_14_out_3));
  assign or_3_out = cancler_8_out_3 | cancler_9_out_3 | cancler_10_out_3 | cancler_11_out_3 | cancler_12_out_3 | cancler_13_out_3 | cancler_14_out_3 | cancler_14_out_3;  // OR_Gate or_3, 16 bits wide
  Register #(.width(16)) register_9 (.D(Data), .en(decoder_1_out23), .clk(CLK), .Q(register_9_q));  // open: clr
  Register #(.width(16)) register_10 (.D(Data), .en(decoder_1_out22), .clk(CLK), .Q(register_10_q));  // open: clr
  Register #(.width(16)) register_11 (.D(Data), .en(decoder_1_out21), .clk(CLK), .Q(register_11_q));  // open: clr
  Register #(.width(16)) register_12 (.D(Data), .en(decoder_1_out20), .clk(CLK), .Q(register_12_q));  // open: clr
  Register #(.width(16)) register_13 (.D(Data), .en(decoder_1_out19), .clk(CLK), .Q(register_13_q));  // open: clr
  Register #(.width(16)) register_14 (.D(Data), .en(decoder_1_out18), .clk(CLK), .Q(register_14_q));  // open: clr
  Register #(.width(16)) register_15 (.D(Data), .en(decoder_1_out17), .clk(CLK), .Q(register_15_q));  // open: clr
  Register #(.width(16)) register_16 (.D(Data), .en(decoder_1_out16), .clk(CLK), .Q(register_16_q));  // open: clr
  Cancler cancler_16 (.Cancle(not_23_out), .Data(register_9_q), .out_3(cancler_16_out_3));
  Cancler cancler_17 (.Cancle(not_22_out), .Data(register_10_q), .out_3(cancler_17_out_3));
  Cancler cancler_18 (.Cancle(not_21_out), .Data(register_11_q), .out_3(cancler_18_out_3));
  Cancler cancler_19 (.Cancle(not_20_out), .Data(register_12_q), .out_3(cancler_19_out_3));
  Cancler cancler_20 (.Cancle(not_19_out), .Data(register_13_q), .out_3(cancler_20_out_3));
  Cancler cancler_21 (.Cancle(not_18_out), .Data(register_14_q), .out_3(cancler_21_out_3));
  Cancler cancler_22 (.Cancle(not_17_out), .Data(register_15_q), .out_3(cancler_22_out_3));
  Cancler cancler_23 (.Cancle(not_16_out), .Data(register_16_q), .out_3(cancler_22_out_3));
  assign or_4_out = cancler_16_out_3 | cancler_17_out_3 | cancler_18_out_3 | cancler_19_out_3 | cancler_20_out_3 | cancler_21_out_3 | cancler_22_out_3 | cancler_22_out_3;  // OR_Gate or_4, 16 bits wide
  Register #(.width(16)) register_17 (.D(Data), .en(decoder_1_out31), .clk(CLK), .Q(register_17_q));  // open: clr
  Register #(.width(16)) register_18 (.D(Data), .en(decoder_1_out30), .clk(CLK), .Q(register_18_q));  // open: clr
  Register #(.width(16)) register_19 (.D(Data), .en(decoder_1_out29), .clk(CLK), .Q(register_19_q));  // open: clr
  Register #(.width(16)) register_20 (.D(Data), .en(decoder_1_out28), .clk(CLK), .Q(register_20_q));  // open: clr
  Register #(.width(16)) register_21 (.D(Data), .en(decoder_1_out27), .clk(CLK), .Q(register_21_q));  // open: clr
  Register #(.width(16)) register_22 (.D(Data), .en(decoder_1_out26), .clk(CLK), .Q(register_22_q));  // open: clr
  Register #(.width(16)) register_23 (.D(Data), .en(decoder_1_out25), .clk(CLK), .Q(register_23_q));  // open: clr
  Register #(.width(16)) register_24 (.D(Data), .en(decoder_1_out24), .clk(CLK), .Q(register_24_q));  // open: clr
  Cancler cancler_24 (.Cancle(not_31_out), .Data(register_17_q), .out_3(cancler_24_out_3));
  Cancler cancler_25 (.Cancle(not_30_out), .Data(register_18_q), .out_3(cancler_25_out_3));
  Cancler cancler_26 (.Cancle(not_29_out), .Data(register_19_q), .out_3(cancler_26_out_3));
  Cancler cancler_27 (.Cancle(not_28_out), .Data(register_20_q), .out_3(cancler_27_out_3));
  Cancler cancler_28 (.Cancle(not_27_out), .Data(register_21_q), .out_3(cancler_28_out_3));
  Cancler cancler_29 (.Cancle(not_26_out), .Data(register_22_q), .out_3(cancler_29_out_3));
  Cancler cancler_30 (.Cancle(not_25_out), .Data(register_23_q), .out_3(cancler_30_out_3));
  Cancler cancler_31 (.Cancle(not_24_out), .Data(register_24_q), .out_3(cancler_30_out_3));
  assign or_5_out = cancler_24_out_3 | cancler_25_out_3 | cancler_26_out_3 | cancler_27_out_3 | cancler_28_out_3 | cancler_29_out_3 | cancler_30_out_3 | cancler_30_out_3;  // OR_Gate or_5, 16 bits wide
  Decoder #(.select(5)) decoder_3 (
    .out1(decoder_3_out1), .out2(decoder_3_out2), .out3(decoder_3_out3), .out4(decoder_3_out4),
    .out5(decoder_3_out5), .out6(decoder_3_out6), .out7(decoder_3_out7), .out8(decoder_3_out8),
    .out9(decoder_3_out9), .out10(decoder_3_out10), .out11(decoder_3_out11), .out12(decoder_3_out12),
    .out13(decoder_3_out13), .out14(decoder_3_out14), .out15(decoder_3_out15), .out16(decoder_3_out16),
    .out17(decoder_3_out17), .out18(decoder_3_out18), .out19(decoder_3_out19), .out20(decoder_3_out20),
    .out21(decoder_3_out21), .out22(decoder_3_out22), .out23(decoder_3_out23), .out24(decoder_3_out24),
    .out25(decoder_3_out25), .out26(decoder_3_out26), .out27(decoder_3_out27), .out28(decoder_3_out28),
    .out29(decoder_3_out29), .out30(decoder_3_out30), .out31(decoder_3_out31), .sel(W), .en(En));  // open: out0
  Decoder #(.select(5)) decoder_4 (
    .out1(decoder_4_out1), .out2(decoder_4_out2), .out3(decoder_4_out3), .out4(decoder_4_out4),
    .out5(decoder_4_out5), .out6(decoder_4_out6), .out7(decoder_4_out7), .out8(decoder_4_out8),
    .out9(decoder_4_out9), .out10(decoder_4_out10), .out11(decoder_4_out11), .out12(decoder_4_out12),
    .out13(decoder_4_out13), .out14(decoder_4_out14), .out15(decoder_4_out15), .out16(decoder_4_out16),
    .out17(decoder_4_out17), .out18(decoder_4_out18), .out19(decoder_4_out19), .out20(decoder_4_out20),
    .out21(decoder_4_out21), .out22(decoder_4_out22), .out23(decoder_4_out23), .out24(decoder_4_out24),
    .out25(decoder_4_out25), .out26(decoder_4_out26), .out27(decoder_4_out27), .out28(decoder_4_out28),
    .out29(decoder_4_out29), .out30(decoder_4_out30), .out31(decoder_4_out31), .sel(R2), .en(En));  // open: out0
  not not_32 (not_32_out, decoder_4_out1);
  not not_33 (not_33_out, decoder_4_out2);
  not not_34 (not_34_out, decoder_4_out3);
  not not_35 (not_35_out, decoder_4_out4);
  not not_36 (not_36_out, decoder_4_out5);
  not not_37 (not_37_out, decoder_4_out6);
  not not_38 (not_38_out, decoder_4_out7);
  not not_39 (not_39_out, decoder_4_out8);
  not not_40 (not_40_out, decoder_4_out9);
  not not_41 (not_41_out, decoder_4_out10);
  not not_42 (not_42_out, decoder_4_out11);
  not not_43 (not_43_out, decoder_4_out12);
  not not_44 (not_44_out, decoder_4_out13);
  not not_45 (not_45_out, decoder_4_out14);
  not not_46 (not_46_out, decoder_4_out15);
  not not_47 (not_47_out, decoder_4_out16);
  not not_48 (not_48_out, decoder_4_out17);
  not not_49 (not_49_out, decoder_4_out18);
  not not_50 (not_50_out, decoder_4_out19);
  not not_51 (not_51_out, decoder_4_out20);
  not not_52 (not_52_out, decoder_4_out21);
  not not_53 (not_53_out, decoder_4_out22);
  not not_54 (not_54_out, decoder_4_out23);
  not not_55 (not_55_out, decoder_4_out24);
  not not_56 (not_56_out, decoder_4_out25);
  not not_57 (not_57_out, decoder_4_out26);
  not not_58 (not_58_out, decoder_4_out27);
  not not_59 (not_59_out, decoder_4_out28);
  not not_60 (not_60_out, decoder_4_out29);
  not not_61 (not_61_out, decoder_4_out30);
  not not_62 (not_62_out, decoder_4_out31);
  Register #(.width(16)) register_25 (.D(Data), .en(decoder_3_out7), .clk(CLK), .Q(register_25_q));  // open: clr
  Register #(.width(16)) register_26 (.D(Data), .en(decoder_3_out6), .clk(CLK), .Q(register_26_q));  // open: clr
  Register #(.width(16)) register_27 (.D(Data), .en(decoder_3_out5), .clk(CLK), .Q(register_27_q));  // open: clr
  Register #(.width(16)) register_28 (.D(Data), .en(decoder_3_out4), .clk(CLK), .Q(register_28_q));  // open: clr
  Register #(.width(16)) register_29 (.D(Data), .en(decoder_3_out3), .clk(CLK), .Q(register_29_q));  // open: clr
  Register #(.width(16)) register_30 (.D(Data), .en(decoder_3_out2), .clk(CLK), .Q(register_30_q));  // open: clr
  Register #(.width(16)) register_31 (.D(Data), .en(decoder_3_out1), .clk(CLK), .Q(register_31_q));  // open: clr
  Cancler cancler_32 (.Cancle(not_38_out), .Data(register_25_q), .out_3(cancler_32_out_3));
  Cancler cancler_33 (.Cancle(not_37_out), .Data(register_26_q), .out_3(cancler_33_out_3));
  Cancler cancler_34 (.Cancle(not_36_out), .Data(register_27_q), .out_3(cancler_34_out_3));
  Cancler cancler_35 (.Cancle(not_35_out), .Data(register_28_q), .out_3(cancler_35_out_3));
  Cancler cancler_36 (.Cancle(not_34_out), .Data(register_29_q), .out_3(cancler_36_out_3));
  Cancler cancler_37 (.Cancle(not_33_out), .Data(register_30_q), .out_3(cancler_37_out_3));
  Cancler cancler_38 (.Cancle(not_32_out), .Data(register_31_q), .out_3(cancler_38_out_3));
  assign or_6_out = cancler_32_out_3 | cancler_33_out_3 | cancler_34_out_3 | cancler_35_out_3 | cancler_36_out_3 | cancler_37_out_3 | cancler_38_out_3;  // OR_Gate or_6, 16 bits wide
  assign R2Out = or_6_out | or_8_out | or_9_out | or_10_out;  // OR_Gate or_7, 16 bits wide
  Register #(.width(16)) register_32 (.D(Data), .en(decoder_3_out15), .clk(CLK), .Q(register_32_q));  // open: clr
  Register #(.width(16)) register_33 (.D(Data), .en(decoder_3_out14), .clk(CLK), .Q(register_33_q));  // open: clr
  Register #(.width(16)) register_34 (.D(Data), .en(decoder_3_out13), .clk(CLK), .Q(register_34_q));  // open: clr
  Register #(.width(16)) register_35 (.D(Data), .en(decoder_3_out12), .clk(CLK), .Q(register_35_q));  // open: clr
  Register #(.width(16)) register_36 (.D(Data), .en(decoder_3_out11), .clk(CLK), .Q(register_36_q));  // open: clr
  Register #(.width(16)) register_37 (.D(Data), .en(decoder_3_out10), .clk(CLK), .Q(register_37_q));  // open: clr
  Register #(.width(16)) register_38 (.D(Data), .en(decoder_3_out9), .clk(CLK), .Q(register_38_q));  // open: clr
  Register #(.width(16)) register_39 (.D(Data), .en(decoder_3_out8), .clk(CLK), .Q(register_39_q));  // open: clr
  Cancler cancler_39 (.Cancle(not_46_out), .Data(register_32_q), .out_3(cancler_39_out_3));
  Cancler cancler_40 (.Cancle(not_45_out), .Data(register_33_q), .out_3(cancler_40_out_3));
  Cancler cancler_41 (.Cancle(not_44_out), .Data(register_34_q), .out_3(cancler_41_out_3));
  Cancler cancler_42 (.Cancle(not_43_out), .Data(register_35_q), .out_3(cancler_42_out_3));
  Cancler cancler_43 (.Cancle(not_42_out), .Data(register_36_q), .out_3(cancler_43_out_3));
  Cancler cancler_44 (.Cancle(not_41_out), .Data(register_37_q), .out_3(cancler_44_out_3));
  Cancler cancler_45 (.Cancle(not_40_out), .Data(register_38_q), .out_3(cancler_45_out_3));
  Cancler cancler_46 (.Cancle(not_39_out), .Data(register_39_q), .out_3(cancler_45_out_3));
  assign or_8_out = cancler_39_out_3 | cancler_40_out_3 | cancler_41_out_3 | cancler_42_out_3 | cancler_43_out_3 | cancler_44_out_3 | cancler_45_out_3 | cancler_45_out_3;  // OR_Gate or_8, 16 bits wide
  Register #(.width(16)) register_40 (.D(Data), .en(decoder_3_out23), .clk(CLK), .Q(register_40_q));  // open: clr
  Register #(.width(16)) register_41 (.D(Data), .en(decoder_3_out22), .clk(CLK), .Q(register_41_q));  // open: clr
  Register #(.width(16)) register_42 (.D(Data), .en(decoder_3_out21), .clk(CLK), .Q(register_42_q));  // open: clr
  Register #(.width(16)) register_43 (.D(Data), .en(decoder_3_out20), .clk(CLK), .Q(register_43_q));  // open: clr
  Register #(.width(16)) register_44 (.D(Data), .en(decoder_3_out19), .clk(CLK), .Q(register_44_q));  // open: clr
  Register #(.width(16)) register_45 (.D(Data), .en(decoder_3_out18), .clk(CLK), .Q(register_45_q));  // open: clr
  Register #(.width(16)) register_46 (.D(Data), .en(decoder_3_out17), .clk(CLK), .Q(register_46_q));  // open: clr
  Register #(.width(16)) register_47 (.D(Data), .en(decoder_3_out16), .clk(CLK), .Q(register_47_q));  // open: clr
  Cancler cancler_47 (.Cancle(not_54_out), .Data(register_40_q), .out_3(cancler_47_out_3));
  Cancler cancler_48 (.Cancle(not_53_out), .Data(register_41_q), .out_3(cancler_48_out_3));
  Cancler cancler_49 (.Cancle(not_52_out), .Data(register_42_q), .out_3(cancler_49_out_3));
  Cancler cancler_50 (.Cancle(not_51_out), .Data(register_43_q), .out_3(cancler_50_out_3));
  Cancler cancler_51 (.Cancle(not_50_out), .Data(register_44_q), .out_3(cancler_51_out_3));
  Cancler cancler_52 (.Cancle(not_49_out), .Data(register_45_q), .out_3(cancler_52_out_3));
  Cancler cancler_53 (.Cancle(not_48_out), .Data(register_46_q), .out_3(cancler_53_out_3));
  Cancler cancler_54 (.Cancle(not_47_out), .Data(register_47_q), .out_3(cancler_53_out_3));
  assign or_9_out = cancler_47_out_3 | cancler_48_out_3 | cancler_49_out_3 | cancler_50_out_3 | cancler_51_out_3 | cancler_52_out_3 | cancler_53_out_3 | cancler_53_out_3;  // OR_Gate or_9, 16 bits wide
  Register #(.width(16)) register_48 (.D(Data), .en(decoder_3_out31), .clk(CLK), .Q(register_48_q));  // open: clr
  Register #(.width(16)) register_49 (.D(Data), .en(decoder_3_out30), .clk(CLK), .Q(register_49_q));  // open: clr
  Register #(.width(16)) register_50 (.D(Data), .en(decoder_3_out29), .clk(CLK), .Q(register_50_q));  // open: clr
  Register #(.width(16)) register_51 (.D(Data), .en(decoder_3_out28), .clk(CLK), .Q(register_51_q));  // open: clr
  Register #(.width(16)) register_52 (.D(Data), .en(decoder_3_out27), .clk(CLK), .Q(register_52_q));  // open: clr
  Register #(.width(16)) register_53 (.D(Data), .en(decoder_3_out26), .clk(CLK), .Q(register_53_q));  // open: clr
  Register #(.width(16)) register_54 (.D(Data), .en(decoder_3_out25), .clk(CLK), .Q(register_54_q));  // open: clr
  Register #(.width(16)) register_55 (.D(Data), .en(decoder_3_out24), .clk(CLK), .Q(register_55_q));  // open: clr
  Cancler cancler_55 (.Cancle(not_62_out), .Data(register_48_q), .out_3(cancler_55_out_3));
  Cancler cancler_56 (.Cancle(not_61_out), .Data(register_49_q), .out_3(cancler_56_out_3));
  Cancler cancler_57 (.Cancle(not_60_out), .Data(register_50_q), .out_3(cancler_57_out_3));
  Cancler cancler_58 (.Cancle(not_59_out), .Data(register_51_q), .out_3(cancler_58_out_3));
  Cancler cancler_59 (.Cancle(not_58_out), .Data(register_52_q), .out_3(cancler_59_out_3));
  Cancler cancler_60 (.Cancle(not_57_out), .Data(register_53_q), .out_3(cancler_60_out_3));
  Cancler cancler_61 (.Cancle(not_56_out), .Data(register_54_q), .out_3(cancler_61_out_3));
  Cancler cancler_62 (.Cancle(not_55_out), .Data(register_55_q), .out_3(cancler_61_out_3));
  assign or_10_out = cancler_55_out_3 | cancler_56_out_3 | cancler_57_out_3 | cancler_58_out_3 | cancler_59_out_3 | cancler_60_out_3 | cancler_61_out_3 | cancler_61_out_3;  // OR_Gate or_10, 16 bits wide
endmodule

module Cancler (
  input  [15:0] Data,
  input  Cancle,
  output [15:0] out_3
);

  wire not_1_out;
  wire [15:0] bit_extender_1_out;

  not not_1 (not_1_out, Cancle);
  assign bit_extender_1_out = {{15{not_1_out}}, not_1_out};  // Bit_Extender bit_extender_1
  assign out_3 = Data & bit_extender_1_out;  // AND_Gate and_1, 16 bits wide
endmodule

module InstMemory (
  input  [19:0] Addr,
  output [31:0] Instruction
);

  ROM #(.addrWidth(20), .dataWidth(32)) four_MB (.addr(Addr), .data(Instruction));

  // Notes on the sheet:
  //   contents of four_MB (hex, n*v repeats v):
  //   14000001 14000022 14000003 8221800 8400800 8601000 184ea600 10800009 4000000 13400003 4000000
endmodule

module ProgramCounter (
  input  [19:0] Address_plus_1,
  input  CLK,
  input  CLR,
  output [19:0] Addr
);

  Register #(.trigger("falling"), .width(20)) register_1 (
    .D(Address_plus_1), .en(1'b1), .clk(CLK), .Q(Addr), .clr(CLR));
endmodule

module ControllUnit (
  input  [5:0] in_1,
  output RegEn,
  output HLT,
  output PC_MUX_bit0,
  output Is_BRH,
  output EnFlagUpdate,
  output Func_MUX,
  output Rs2_MUX,
  output Dest_MUX,
  output [4:0] Imm_operation_func,
  output EN_SHFT,
  output EN_PUSH,
  output PC_MUX_bit1,
  output DataMem_EN,
  output DataMem_WE,
  output NoW,
  output Data_MUX,
  output Reg_Rs2_MUX
);

  wire decoder_1_out2, decoder_1_out3, decoder_1_out5, decoder_1_out6, decoder_1_out7, decoder_1_out8,
       decoder_1_out9, decoder_1_out10, decoder_1_out11, decoder_1_out12, decoder_1_out13, decoder_1_out14,
       decoder_1_out15, decoder_1_out16, decoder_1_out17;

  Decoder #(.select(6)) decoder_1 (
    .out1(HLT), .out2(decoder_1_out2), .out3(decoder_1_out3), .out4(Is_BRH), .out5(decoder_1_out5),
    .out6(decoder_1_out6), .out7(decoder_1_out7), .out8(decoder_1_out8), .out9(decoder_1_out9),
    .out10(decoder_1_out10), .out11(decoder_1_out11), .out12(decoder_1_out12), .out13(decoder_1_out13),
    .out14(decoder_1_out14), .out15(decoder_1_out15), .out16(decoder_1_out16), .out17(decoder_1_out17),
    .out18(Imm_operation_func[4]), .out19(EN_PUSH), .out20(PC_MUX_bit1), .out21(Data_MUX),
    .out22(DataMem_WE), .sel(in_1), .en(1'b1));  // open: out0, out23, out24, out25, out26, out27, out28, out29, out30, out31, out32, out33, out34, out35, out36, out37, out38, out39, out40, out41, out42, out43, out44, out45, out46, out47, out48, out49, out50, out51, out52, out53, out54, out55, out56, out57, out58, out59, out60, out61, out62, out63
  or or_1 (Dest_MUX, decoder_1_out5, decoder_1_out6, decoder_1_out7, decoder_1_out8, decoder_1_out9, decoder_1_out10, decoder_1_out11, decoder_1_out12, decoder_1_out13, decoder_1_out14, decoder_1_out15, decoder_1_out16, decoder_1_out17, Imm_operation_func[4], Data_MUX, DataMem_WE);
  or or_2 (RegEn, decoder_1_out2, Dest_MUX);
  or or_3 (PC_MUX_bit0, decoder_1_out3, EN_PUSH);
  or or_4 (Imm_operation_func[0], decoder_1_out11, decoder_1_out13, decoder_1_out6, decoder_1_out8, decoder_1_out10, decoder_1_out15, decoder_1_out17);
  or or_5 (Imm_operation_func[1], decoder_1_out7, decoder_1_out13, decoder_1_out8, decoder_1_out12, decoder_1_out16, decoder_1_out17);
  or or_6 (Imm_operation_func[2], decoder_1_out15, decoder_1_out9, decoder_1_out10, decoder_1_out14, decoder_1_out16, decoder_1_out17);
  or or_7 (Imm_operation_func[3], decoder_1_out15, decoder_1_out11, decoder_1_out12, decoder_1_out16, decoder_1_out13, decoder_1_out14, decoder_1_out17);
  or or_8 (EN_SHFT, EN_PUSH, PC_MUX_bit1);
  or or_9 (DataMem_EN, Data_MUX, DataMem_WE);
  or or_10 (EnFlagUpdate, decoder_1_out2, decoder_1_out5, decoder_1_out6, decoder_1_out9, decoder_1_out7, decoder_1_out8, decoder_1_out10);

  assign Func_MUX = Dest_MUX;
  assign NoW = DataMem_WE;
  assign Reg_Rs2_MUX = DataMem_WE;
  assign Rs2_MUX = Dest_MUX;
endmodule

module test (
);

  Cancler cancler_1 ();  // open: Cancle, Data, out_3
endmodule

module FlagChecker (
  input  V_Flag,
  input  N_Flag,
  input  C_Flag,
  input  Z_Flag,
  input  [3:0] COND,
  output TrueOrFalse
);

  wire and_1_out, not_1_out, not_2_out, not_3_out, not_4_out, not_5_out, or_1_out, or_2_out, or_3_out,
       xor_1_out;

  not not_1 (not_1_out, C_Flag);
  xor xor_1 (xor_1_out, V_Flag, N_Flag);
  or or_1 (or_1_out, xor_1_out, Z_Flag);
  or or_2 (or_2_out, not_1_out, Z_Flag);
  or or_3 (or_3_out, C_Flag, not_3_out);
  not not_2 (not_2_out, xor_1_out);
  and and_1 (and_1_out, not_2_out, not_3_out);
  not not_3 (not_3_out, Z_Flag);
  Multiplexer #(.select(4)) multiplexer_1 (
    .in0(Z_Flag), .in1(not_3_out), .in2(xor_1_out), .in3(not_2_out), .in4(or_1_out), .in5(and_1_out),
    .in6(not_1_out), .in7(C_Flag), .in8(or_2_out), .in9(or_3_out), .in10(N_Flag), .in11(not_4_out),
    .in12(V_Flag), .in13(not_5_out), .in14(1'b1), .in15(1'b0), .out(TrueOrFalse), .sel(COND));
  not not_4 (not_4_out, N_Flag);
  not not_5 (not_5_out, V_Flag);
endmodule

module BidirectionalShiftRegister (
  input  PopOrPush,
  input  ShiftInput,
  input  CLK,
  input  EnableShift,
  output PopOut
);

  wire and_1_out, and_2_out, and_3_out, and_4_out, and_5_out, and_6_out, and_7_out, and_8_out, and_9_out,
       and_10_out, and_11_out, and_12_out, and_13_out, and_14_out, and_15_out, and_16_out, and_17_out,
       and_18_out, and_19_out, and_20_out, and_21_out, and_22_out, and_23_out, and_24_out, and_25_out,
       and_26_out, and_27_out, and_28_out, and_29_out, and_30_out, and_31_out, and_32_out, and_33_out,
       and_34_out, and_35_out, and_36_out, and_37_out, and_38_out, and_39_out, and_40_out, and_41_out,
       and_42_out, and_43_out, and_44_out, and_45_out, and_46_out, and_47_out, and_48_out, and_49_out,
       and_50_out, and_51_out, and_52_out, and_53_out, and_54_out, and_55_out, and_56_out, and_57_out,
       and_58_out, and_59_out, and_60_out, and_61_out, and_62_out, and_63_out, and_64_out, and_65_out,
       and_66_out, and_67_out, d_ff_2_q, d_ff_3_q, d_ff_4_q, d_ff_5_q, d_ff_6_q, d_ff_7_q, d_ff_8_q,
       d_ff_9_q, d_ff_10_q, d_ff_11_q, d_ff_12_q, d_ff_13_q, d_ff_14_q, d_ff_15_q, d_ff_16_q, d_ff_17_q,
       d_ff_18_q, d_ff_19_q, d_ff_20_q, d_ff_21_q, d_ff_22_q, d_ff_23_q, d_ff_24_q, d_ff_25_q, d_ff_26_q,
       d_ff_27_q, d_ff_28_q, d_ff_29_q, d_ff_30_q, d_ff_31_q, d_ff_32_q, d_ff_33_q, not_1_out, or_1_out,
       or_2_out, or_3_out, or_4_out, or_5_out, or_6_out, or_7_out, or_8_out, or_9_out, or_10_out, or_11_out,
       or_12_out, or_13_out, or_14_out, or_15_out, or_16_out, or_17_out, or_18_out, or_19_out, or_20_out,
       or_21_out, or_22_out, or_23_out, or_24_out, or_25_out, or_26_out, or_27_out, or_28_out, or_29_out,
       or_30_out, or_31_out, or_32_out, or_33_out;

  not not_1 (not_1_out, PopOrPush);
  and and_1 (and_1_out, CLK, EnableShift);
  and and_2 (and_2_out, 1'b0, PopOrPush);
  and and_3 (and_3_out, not_1_out, d_ff_2_q);
  or or_1 (or_1_out, and_2_out, and_3_out);
  D_Flip_Flop d_ff_1 (.D(or_1_out), .clk(and_1_out), .Q(PopOut));  // open: Qn, preset, reset
  and and_4 (and_4_out, ShiftInput, PopOrPush);
  or or_2 (or_2_out, and_4_out, and_5_out);
  and and_5 (and_5_out, not_1_out, d_ff_3_q);
  D_Flip_Flop d_ff_2 (.D(or_2_out), .clk(and_1_out), .Q(d_ff_2_q));  // open: Qn, preset, reset
  and and_6 (and_6_out, d_ff_2_q, PopOrPush);
  and and_7 (and_7_out, not_1_out, d_ff_4_q);
  or or_3 (or_3_out, and_6_out, and_7_out);
  D_Flip_Flop d_ff_3 (.D(or_3_out), .clk(and_1_out), .Q(d_ff_3_q));  // open: Qn, preset, reset
  and and_8 (and_8_out, d_ff_3_q, PopOrPush);
  and and_9 (and_9_out, not_1_out, d_ff_5_q);
  or or_4 (or_4_out, and_8_out, and_9_out);
  D_Flip_Flop d_ff_4 (.D(or_4_out), .clk(and_1_out), .Q(d_ff_4_q));  // open: Qn, preset, reset
  and and_10 (and_10_out, not_1_out, d_ff_6_q);
  and and_11 (and_11_out, d_ff_4_q, PopOrPush);
  or or_5 (or_5_out, and_11_out, and_10_out);
  D_Flip_Flop d_ff_5 (.D(or_5_out), .clk(and_1_out), .Q(d_ff_5_q));  // open: Qn, preset, reset
  and and_12 (and_12_out, d_ff_5_q, PopOrPush);
  and and_13 (and_13_out, not_1_out, d_ff_7_q);
  or or_6 (or_6_out, and_12_out, and_13_out);
  D_Flip_Flop d_ff_6 (.D(or_6_out), .clk(and_1_out), .Q(d_ff_6_q));  // open: Qn, preset, reset
  and and_14 (and_14_out, d_ff_6_q, PopOrPush);
  or or_7 (or_7_out, and_14_out, and_15_out);
  and and_15 (and_15_out, not_1_out, d_ff_8_q);
  D_Flip_Flop d_ff_7 (.D(or_7_out), .clk(and_1_out), .Q(d_ff_7_q));  // open: Qn, preset, reset
  and and_16 (and_16_out, d_ff_7_q, PopOrPush);
  and and_17 (and_17_out, not_1_out, d_ff_9_q);
  or or_8 (or_8_out, and_16_out, and_17_out);
  D_Flip_Flop d_ff_8 (.D(or_8_out), .clk(and_1_out), .Q(d_ff_8_q));  // open: Qn, preset, reset
  and and_18 (and_18_out, d_ff_8_q, PopOrPush);
  and and_19 (and_19_out, not_1_out, d_ff_10_q);
  or or_9 (or_9_out, and_18_out, and_19_out);
  D_Flip_Flop d_ff_9 (.D(or_9_out), .clk(and_1_out), .Q(d_ff_9_q));  // open: Qn, preset, reset
  and and_20 (and_20_out, d_ff_9_q, PopOrPush);
  or or_10 (or_10_out, and_20_out, and_21_out);
  and and_21 (and_21_out, not_1_out, d_ff_11_q);
  D_Flip_Flop d_ff_10 (.D(or_10_out), .clk(and_1_out), .Q(d_ff_10_q));  // open: Qn, preset, reset
  and and_22 (and_22_out, d_ff_10_q, PopOrPush);
  and and_23 (and_23_out, not_1_out, d_ff_12_q);
  or or_11 (or_11_out, and_22_out, and_23_out);
  D_Flip_Flop d_ff_11 (.D(or_11_out), .clk(and_1_out), .Q(d_ff_11_q));  // open: Qn, preset, reset
  and and_24 (and_24_out, d_ff_11_q, PopOrPush);
  and and_25 (and_25_out, not_1_out, d_ff_13_q);
  or or_12 (or_12_out, and_24_out, and_25_out);
  D_Flip_Flop d_ff_12 (.D(or_12_out), .clk(and_1_out), .Q(d_ff_12_q));  // open: Qn, preset, reset
  and and_26 (and_26_out, d_ff_12_q, PopOrPush);
  and and_27 (and_27_out, not_1_out, d_ff_14_q);
  or or_13 (or_13_out, and_26_out, and_27_out);
  D_Flip_Flop d_ff_13 (.D(or_13_out), .clk(and_1_out), .Q(d_ff_13_q));  // open: Qn, preset, reset
  and and_28 (and_28_out, d_ff_13_q, PopOrPush);
  and and_29 (and_29_out, not_1_out, d_ff_15_q);
  or or_14 (or_14_out, and_28_out, and_29_out);
  D_Flip_Flop d_ff_14 (.D(or_14_out), .clk(and_1_out), .Q(d_ff_14_q));  // open: Qn, preset, reset
  and and_30 (and_30_out, d_ff_14_q, PopOrPush);
  or or_15 (or_15_out, and_30_out, and_31_out);
  and and_31 (and_31_out, not_1_out, d_ff_16_q);
  D_Flip_Flop d_ff_15 (.D(or_15_out), .clk(and_1_out), .Q(d_ff_15_q));  // open: Qn, preset, reset
  and and_32 (and_32_out, d_ff_15_q, PopOrPush);
  and and_33 (and_33_out, not_1_out, d_ff_17_q);
  or or_16 (or_16_out, and_32_out, and_33_out);
  D_Flip_Flop d_ff_16 (.D(or_16_out), .clk(and_1_out), .Q(d_ff_16_q));  // open: Qn, preset, reset
  and and_34 (and_34_out, d_ff_16_q, PopOrPush);
  and and_35 (and_35_out, not_1_out, d_ff_18_q);
  or or_17 (or_17_out, and_34_out, and_35_out);
  D_Flip_Flop d_ff_17 (.D(or_17_out), .clk(and_1_out), .Q(d_ff_17_q));  // open: Qn, preset, reset
  and and_36 (and_36_out, d_ff_17_q, PopOrPush);
  or or_18 (or_18_out, and_36_out, and_37_out);
  and and_37 (and_37_out, not_1_out, d_ff_19_q);
  D_Flip_Flop d_ff_18 (.D(or_18_out), .clk(and_1_out), .Q(d_ff_18_q));  // open: Qn, preset, reset
  and and_38 (and_38_out, d_ff_18_q, PopOrPush);
  and and_39 (and_39_out, not_1_out, d_ff_20_q);
  or or_19 (or_19_out, and_38_out, and_39_out);
  D_Flip_Flop d_ff_19 (.D(or_19_out), .clk(and_1_out), .Q(d_ff_19_q));  // open: Qn, preset, reset
  and and_40 (and_40_out, d_ff_19_q, PopOrPush);
  and and_41 (and_41_out, not_1_out, d_ff_21_q);
  or or_20 (or_20_out, and_40_out, and_41_out);
  D_Flip_Flop d_ff_20 (.D(or_20_out), .clk(and_1_out), .Q(d_ff_20_q));  // open: Qn, preset, reset
  and and_42 (and_42_out, d_ff_20_q, PopOrPush);
  and and_43 (and_43_out, not_1_out, d_ff_22_q);
  or or_21 (or_21_out, and_42_out, and_43_out);
  D_Flip_Flop d_ff_21 (.D(or_21_out), .clk(and_1_out), .Q(d_ff_21_q));  // open: Qn, preset, reset
  and and_44 (and_44_out, d_ff_21_q, PopOrPush);
  and and_45 (and_45_out, not_1_out, d_ff_23_q);
  or or_22 (or_22_out, and_44_out, and_45_out);
  D_Flip_Flop d_ff_22 (.D(or_22_out), .clk(and_1_out), .Q(d_ff_22_q));  // open: Qn, preset, reset
  and and_46 (and_46_out, d_ff_22_q, PopOrPush);
  or or_23 (or_23_out, and_46_out, and_47_out);
  and and_47 (and_47_out, not_1_out, d_ff_24_q);
  D_Flip_Flop d_ff_23 (.D(or_23_out), .clk(and_1_out), .Q(d_ff_23_q));  // open: Qn, preset, reset
  and and_48 (and_48_out, d_ff_23_q, PopOrPush);
  and and_49 (and_49_out, not_1_out, d_ff_25_q);
  or or_24 (or_24_out, and_48_out, and_49_out);
  D_Flip_Flop d_ff_24 (.D(or_24_out), .clk(and_1_out), .Q(d_ff_24_q));  // open: Qn, preset, reset
  and and_50 (and_50_out, d_ff_24_q, PopOrPush);
  and and_51 (and_51_out, not_1_out, d_ff_26_q);
  or or_25 (or_25_out, and_50_out, and_51_out);
  D_Flip_Flop d_ff_25 (.D(or_25_out), .clk(and_1_out), .Q(d_ff_25_q));  // open: Qn, preset, reset
  and and_52 (and_52_out, d_ff_25_q, PopOrPush);
  or or_26 (or_26_out, and_52_out, and_53_out);
  and and_53 (and_53_out, not_1_out, d_ff_27_q);
  D_Flip_Flop d_ff_26 (.D(or_26_out), .clk(and_1_out), .Q(d_ff_26_q));  // open: Qn, preset, reset
  and and_54 (and_54_out, d_ff_26_q, PopOrPush);
  and and_55 (and_55_out, not_1_out, d_ff_28_q);
  or or_27 (or_27_out, and_54_out, and_55_out);
  D_Flip_Flop d_ff_27 (.D(or_27_out), .clk(and_1_out), .Q(d_ff_27_q));  // open: Qn, preset, reset
  and and_56 (and_56_out, d_ff_27_q, PopOrPush);
  and and_57 (and_57_out, not_1_out, d_ff_29_q);
  or or_28 (or_28_out, and_56_out, and_57_out);
  D_Flip_Flop d_ff_28 (.D(or_28_out), .clk(and_1_out), .Q(d_ff_28_q));  // open: Qn, preset, reset
  and and_58 (and_58_out, d_ff_28_q, PopOrPush);
  and and_59 (and_59_out, not_1_out, d_ff_30_q);
  or or_29 (or_29_out, and_58_out, and_59_out);
  D_Flip_Flop d_ff_29 (.D(or_29_out), .clk(and_1_out), .Q(d_ff_29_q));  // open: Qn, preset, reset
  and and_60 (and_60_out, d_ff_29_q, PopOrPush);
  and and_61 (and_61_out, not_1_out, d_ff_31_q);
  or or_30 (or_30_out, and_60_out, and_61_out);
  D_Flip_Flop d_ff_30 (.D(or_30_out), .clk(and_1_out), .Q(d_ff_30_q));  // open: Qn, preset, reset
  and and_62 (and_62_out, d_ff_30_q, PopOrPush);
  or or_31 (or_31_out, and_62_out, and_63_out);
  and and_63 (and_63_out, not_1_out, d_ff_32_q);
  D_Flip_Flop d_ff_31 (.D(or_31_out), .clk(and_1_out), .Q(d_ff_31_q));  // open: Qn, preset, reset
  and and_64 (and_64_out, d_ff_31_q, PopOrPush);
  and and_65 (and_65_out, not_1_out, d_ff_33_q);
  or or_32 (or_32_out, and_64_out, and_65_out);
  D_Flip_Flop d_ff_32 (.D(or_32_out), .clk(and_1_out), .Q(d_ff_32_q));  // open: Qn, preset, reset
  and and_66 (and_66_out, d_ff_32_q, PopOrPush);
  and and_67 (and_67_out, not_1_out, ShiftInput);
  or or_33 (or_33_out, and_66_out, and_67_out);
  D_Flip_Flop d_ff_33 (.D(or_33_out), .clk(and_1_out), .Q(d_ff_33_q));  // open: Qn, preset, reset
endmodule

module CallStack (
  input  PopOrPush,
  input  [19:0] DataInput,
  input  CLK,
  input  EnShift,
  output [19:0] PopOut
);

  BidirectionalShiftRegister bidirectionalshiftregister_1 (
    .CLK(CLK), .EnableShift(EnShift), .PopOrPush(PopOrPush), .ShiftInput(DataInput[0]), .PopOut(PopOut[0]));
  BidirectionalShiftRegister bidirectionalshiftregister_2 (
    .CLK(CLK), .EnableShift(EnShift), .PopOrPush(PopOrPush), .ShiftInput(DataInput[1]), .PopOut(PopOut[1]));
  BidirectionalShiftRegister bidirectionalshiftregister_3 (
    .CLK(CLK), .EnableShift(EnShift), .PopOrPush(PopOrPush), .ShiftInput(DataInput[2]), .PopOut(PopOut[2]));
  BidirectionalShiftRegister bidirectionalshiftregister_4 (
    .CLK(CLK), .EnableShift(EnShift), .PopOrPush(PopOrPush), .ShiftInput(DataInput[3]), .PopOut(PopOut[3]));
  BidirectionalShiftRegister bidirectionalshiftregister_5 (
    .CLK(CLK), .EnableShift(EnShift), .PopOrPush(PopOrPush), .ShiftInput(DataInput[4]), .PopOut(PopOut[4]));
  BidirectionalShiftRegister bidirectionalshiftregister_6 (
    .CLK(CLK), .EnableShift(EnShift), .PopOrPush(PopOrPush), .ShiftInput(DataInput[5]), .PopOut(PopOut[5]));
  BidirectionalShiftRegister bidirectionalshiftregister_7 (
    .CLK(CLK), .EnableShift(EnShift), .PopOrPush(PopOrPush), .ShiftInput(DataInput[6]), .PopOut(PopOut[6]));
  BidirectionalShiftRegister bidirectionalshiftregister_8 (
    .CLK(CLK), .EnableShift(EnShift), .PopOrPush(PopOrPush), .ShiftInput(DataInput[7]), .PopOut(PopOut[7]));
  BidirectionalShiftRegister bidirectionalshiftregister_9 (
    .CLK(CLK), .EnableShift(EnShift), .PopOrPush(PopOrPush), .ShiftInput(DataInput[8]), .PopOut(PopOut[8]));
  BidirectionalShiftRegister bidirectionalshiftregister_10 (
    .CLK(CLK), .EnableShift(EnShift), .PopOrPush(PopOrPush), .ShiftInput(DataInput[9]), .PopOut(PopOut[9]));
  BidirectionalShiftRegister bidirectionalshiftregister_11 (
    .CLK(CLK), .EnableShift(EnShift), .PopOrPush(PopOrPush), .ShiftInput(DataInput[10]), .PopOut(PopOut[10]));
  BidirectionalShiftRegister bidirectionalshiftregister_12 (
    .CLK(CLK), .EnableShift(EnShift), .PopOrPush(PopOrPush), .ShiftInput(DataInput[11]), .PopOut(PopOut[11]));
  BidirectionalShiftRegister bidirectionalshiftregister_13 (
    .CLK(CLK), .EnableShift(EnShift), .PopOrPush(PopOrPush), .ShiftInput(DataInput[12]), .PopOut(PopOut[12]));
  BidirectionalShiftRegister bidirectionalshiftregister_14 (
    .CLK(CLK), .EnableShift(EnShift), .PopOrPush(PopOrPush), .ShiftInput(DataInput[13]), .PopOut(PopOut[13]));
  BidirectionalShiftRegister bidirectionalshiftregister_15 (
    .CLK(CLK), .EnableShift(EnShift), .PopOrPush(PopOrPush), .ShiftInput(DataInput[14]), .PopOut(PopOut[14]));
  BidirectionalShiftRegister bidirectionalshiftregister_16 (
    .CLK(CLK), .EnableShift(EnShift), .PopOrPush(PopOrPush), .ShiftInput(DataInput[15]), .PopOut(PopOut[15]));
  BidirectionalShiftRegister bidirectionalshiftregister_17 (
    .CLK(CLK), .EnableShift(EnShift), .PopOrPush(PopOrPush), .ShiftInput(DataInput[16]), .PopOut(PopOut[16]));
  BidirectionalShiftRegister bidirectionalshiftregister_18 (
    .CLK(CLK), .EnableShift(EnShift), .PopOrPush(PopOrPush), .ShiftInput(DataInput[17]), .PopOut(PopOut[17]));
  BidirectionalShiftRegister bidirectionalshiftregister_19 (
    .CLK(CLK), .EnableShift(EnShift), .PopOrPush(PopOrPush), .ShiftInput(DataInput[18]), .PopOut(PopOut[18]));
  BidirectionalShiftRegister bidirectionalshiftregister_20 (
    .CLK(CLK), .EnableShift(EnShift), .PopOrPush(PopOrPush), .ShiftInput(DataInput[19]), .PopOut(PopOut[19]));
endmodule

module DataMemory (
  input  [15:0] Address,
  input  [15:0] Data,
  input  WE,
  input  CLK,
  input  EN,
  output [15:0] out_6
);

  wire and_1_out;

  and and_1 (and_1_out, CLK, EN);
  RAM #(.addrWidth(16), .dataWidth(16), .enables("line")) ram_1 (
    .addr(Address), .we(WE), .clk(and_1_out), .din(Data), .dout(out_6));
endmodule
